# Fritzing sketch Su_Sensor (saved by Fritzing 0.9.10b)

parts:
  Parça1 = Arduino Uno (Rev3)
  Water_Level_Sensor1 = Water Level Sensor

nets:
  N1: Parça1.A0, Water_Level_Sensor1.SIG
  5V: Parça1.5V, Water_Level_Sensor1.VCC
  GND: Parça1.GND, Water_Level_Sensor1.GND

custom parts:
  Water Level Sensor: A water level sensor. This sensor operates at 3V to 5V. The Sig (signal) pin outputs an analogue signal that is in proportion to the amount of water in contact with the sensor.
