# Fritzing sketch L298N_arduioo_kullanımı (saved by Fritzing 0.9.10b)

parts:
  Parça1 = Arduino Uno (Rev3)
  S1 = H-Bridge with L298N
  BAT1 = BC9VPC [package=bc9vpc]
  M1 = gear-motor
  M2 = gear-motor

nets:
  N1: Parça1.D8, S1.IN1
  N2: Parça1.D9_PWM, S1.ENA
  N3: Parça1.D3_PWM, S1.ENB
  N4: Parça1.D5_PWM, S1.IN4
  N5: Parça1.D6_PWM, S1.IN3
  N6: Parça1.D7, S1.IN2
  GND: Parça1.GND, S1.GND, BAT1.V-
  VIN: Parça1.VIN, S1.12V, BAT1.V+
  N7: S1.M1-01, M1.pin_2
  N8: S1.M1-02, M1.pin_1
  N9: S1.M2-01, M2.pin_1
  N10: S1.M2-02, M2.pin_2

notes:
  en az 12V kullanmak tavsiye edilir

custom parts:
  H-Bridge with L298N: h-bridge
