# Fritzing sketch MZ80-Cisim-Sensor (saved by Fritzing 0.9.10b)

parts:
  M1 = E18-D80NK_1 [package=THT]
  Parça2 = Arduino Uno (Rev3)

nets:
  N1: M1.pin1, Parça2.GND
  N2: M1.pin2, Parça2.5V
  N3: M1.pin3, Parça2.D3_PWM

custom parts:
  E18-D80NK_1: E18-D80NK Proximity Sensor module.
